// Logisim project Projeto_SD_V01.circ as structural Verilog
module Via_de_Dados (
  input  [31:0] A,
  input  in_2,
  input  [3:0] OperCode,
  input  [31:0] B,
  input  [4:0] SelRegW,
  input  [4:0] SelRegA,
  input  [4:0] SelRegB,
  input  [3:0] OperCode_2,
  input  [31:0] DATA_IN,
  input  in_10,
  input  [4:0] SelRegW_2,
  input  [4:0] SelRegA_2,
  input  [4:0] SelRegB_2,
  output [31:0] Result,
  output [31:0] DataA,
  output [31:0] DataB
);

  wire [31:0] banco_registrador_32_2_datarega, banco_registrador_32_2_dataregb, ula_32_2_result;

  Banco_Registrador_32 banco_registrador_32_1 (
    .WR(in_10), .DataRegA(DataA), .DataRegB(DataB), .DATA_IN_32(DATA_IN), .SelRegW(SelRegW_2),
    .SelRegA(SelRegA_2), .SelRegB(SelRegB_2));
  ULA_32 ula_32_1 (.A(A), .B(B), .Result(Result), .OperCode(OperCode_2));
  NOTAS notas_1 ();
  Banco_Registrador_32 banco_registrador_32_2 (
    .WR(in_2), .DataRegA(banco_registrador_32_2_datarega), .DataRegB(banco_registrador_32_2_dataregb),
    .DATA_IN_32(ula_32_2_result), .SelRegW(SelRegW), .SelRegA(SelRegA), .SelRegB(SelRegB));
  ULA_32 ula_32_2 (
    .A(banco_registrador_32_2_datarega), .B(banco_registrador_32_2_dataregb), .Result(ula_32_2_result),
    .OperCode(OperCode));
endmodule

// MUX-2
module MUX_2 (
  input  Canal_0,
  input  Canal_1,
  input  Seletor,
  output \Saída 
);

  wire and_1_out, and_2_out;

  and and_1 (and_1_out, Canal_0, ~Seletor);  // AND_Gate
  and and_2 (and_2_out, Canal_1, Seletor);
  or or_1 (\Saída , and_1_out, and_2_out);
endmodule

// MUX-16
module MUX_16 (
  input  Canal_0,
  input  Canal_1,
  input  Canal_2,
  input  Canal_3,
  input  Canal_4,
  input  Canal_5,
  input  Canal_6,
  input  Canal_7,
  input  Canal_8,
  input  Canal_9,
  input  Canal_10,
  input  Canal_11,
  input  Canal_12,
  input  Canal_13,
  input  Canal_14,
  input  Canal_15,
  input  Sel_3,
  input  Sel2,
  input  Sel1,
  input  Sel_0,
  output \Saída 
);

  wire \mux_2_1_saída , \mux_2_2_saída , \mux_2_3_saída , \mux_2_4_saída , \mux_2_5_saída , \mux_2_6_saída ,
       \mux_2_7_saída , \mux_2_8_saída , \mux_2_9_saída , \mux_2_10_saída , \mux_2_11_saída ,
       \mux_2_12_saída , \mux_2_13_saída , \mux_2_14_saída ;

  MUX_2 mux_2_1 (.Canal_0(Canal_0), .Canal_1(Canal_1), .\Saída (\mux_2_1_saída ), .Seletor(Sel_0));
  MUX_2 mux_2_2 (.Canal_0(Canal_2), .Canal_1(Canal_3), .\Saída (\mux_2_2_saída ), .Seletor(Sel_0));
  MUX_2 mux_2_3 (.Canal_0(Canal_4), .Canal_1(Canal_5), .\Saída (\mux_2_3_saída ), .Seletor(Sel_0));
  MUX_2 mux_2_4 (.Canal_0(Canal_6), .Canal_1(Canal_7), .\Saída (\mux_2_4_saída ), .Seletor(Sel_0));
  MUX_2 mux_2_5 (.Canal_0(Canal_8), .Canal_1(Canal_9), .\Saída (\mux_2_5_saída ), .Seletor(Sel_0));
  MUX_2 mux_2_6 (.Canal_0(Canal_10), .Canal_1(Canal_11), .\Saída (\mux_2_6_saída ), .Seletor(Sel_0));
  MUX_2 mux_2_7 (.Canal_0(Canal_12), .Canal_1(Canal_13), .\Saída (\mux_2_7_saída ), .Seletor(Sel_0));
  MUX_2 mux_2_8 (.Canal_0(Canal_14), .Canal_1(Canal_15), .\Saída (\mux_2_8_saída ), .Seletor(Sel_0));
  MUX_2 mux_2_9 (.Canal_0(\mux_2_1_saída ), .Canal_1(\mux_2_2_saída ), .\Saída (\mux_2_9_saída ), .Seletor(Sel1));
  MUX_2 mux_2_10 (.Canal_0(\mux_2_3_saída ), .Canal_1(\mux_2_4_saída ), .\Saída (\mux_2_10_saída ), .Seletor(Sel1));
  MUX_2 mux_2_11 (.Canal_0(\mux_2_5_saída ), .Canal_1(\mux_2_6_saída ), .\Saída (\mux_2_11_saída ), .Seletor(Sel1));
  MUX_2 mux_2_12 (.Canal_0(\mux_2_7_saída ), .Canal_1(\mux_2_8_saída ), .\Saída (\mux_2_12_saída ), .Seletor(Sel1));
  MUX_2 mux_2_13 (.Canal_0(\mux_2_9_saída ), .Canal_1(\mux_2_10_saída ), .\Saída (\mux_2_13_saída ), .Seletor(Sel2));
  MUX_2 mux_2_14 (.Canal_0(\mux_2_11_saída ), .Canal_1(\mux_2_12_saída ), .\Saída (\mux_2_14_saída ), .Seletor(Sel2));
  MUX_2 mux_2_15 (.Canal_0(\mux_2_13_saída ), .Canal_1(\mux_2_14_saída ), .\Saída (\Saída ), .Seletor(Sel_3));
endmodule

// SoC
module Somador_Completo (
  input  a,
  input  b,
  input  Te_SoC,
  output Ts_SoC,
  output Soma
);

  wire and_1_out, and_2_out, and_3_out, xor_1_out;

  or or_1 (Ts_SoC, and_1_out, and_2_out, and_3_out);
  and and_1 (and_1_out, a, Te_SoC);
  and and_2 (and_2_out, a, b);
  and and_3 (and_3_out, b, Te_SoC);
  xor xor_1 (xor_1_out, a, b);
  xor xor_2 (Soma, Te_SoC, xor_1_out);
endmodule

// SbC
module Subtrator_Completo (
  input  a,
  input  b,
  input  Te_SubC,
  output Ts_SubC,
  output Diff
);

  wire and_1_out, and_2_out, and_3_out, xor_1_out;

  or or_1 (Ts_SubC, and_1_out, and_2_out, and_3_out);
  and and_1 (and_1_out, ~a, Te_SubC);  // AND_Gate
  and and_2 (and_2_out, ~a, b);  // AND_Gate
  and and_3 (and_3_out, b, Te_SubC);
  xor xor_1 (xor_1_out, a, b);
  xor xor_2 (Diff, Te_SubC, xor_1_out);
endmodule

// C'2
module COMPLEMENTO_2 (
  input  B,
  input  Seletor,
  output \Saída 
);

  wire not_1_out;

  not not_1 (not_1_out, B);
  MUX_2 mux_2_1 (.Canal_0(B), .Canal_1(not_1_out), .\Saída (\Saída ), .Seletor(Seletor));
endmodule

// SEL-C'2
module SEL_COMPLEMENTO_2 (
  input  [3:0] OperCode,
  output Activation
);

  and and_1 (Activation, OperCode[3], OperCode[2], OperCode[1], OperCode[0]);
endmodule

// CIN-32
module CIN_32 (
  input  [31:0] Entrada,
  output Bit_0,
  output Bit_1,
  output Bit_2,
  output Bit_3,
  output Bit_4,
  output Bit_5,
  output Bit_6,
  output Bit_7,
  output Bit_8,
  output Bit_9,
  output Bit_10,
  output Bit_11,
  output Bit_12,
  output Bit_13,
  output Bit_14,
  output Bit_15,
  output Bit_16,
  output Bit_17,
  output Bit_18,
  output Bit_19,
  output Bit_20,
  output Bit_21,
  output Bit_22,
  output Bit_23,
  output Bit_24,
  output Bit_25,
  output Bit_26,
  output Bit_27,
  output Bit_28,
  output Bit_29,
  output Bit_30,
  output Bit_31
);


  assign Bit_0 = Entrada[0];
  assign Bit_1 = Entrada[1];
  assign Bit_2 = Entrada[2];
  assign Bit_3 = Entrada[3];
  assign Bit_4 = Entrada[4];
  assign Bit_5 = Entrada[5];
  assign Bit_6 = Entrada[6];
  assign Bit_7 = Entrada[7];
  assign Bit_8 = Entrada[8];
  assign Bit_9 = Entrada[9];
  assign Bit_10 = Entrada[10];
  assign Bit_11 = Entrada[11];
  assign Bit_12 = Entrada[12];
  assign Bit_13 = Entrada[13];
  assign Bit_14 = Entrada[14];
  assign Bit_15 = Entrada[15];
  assign Bit_16 = Entrada[16];
  assign Bit_17 = Entrada[17];
  assign Bit_18 = Entrada[18];
  assign Bit_19 = Entrada[19];
  assign Bit_20 = Entrada[20];
  assign Bit_21 = Entrada[21];
  assign Bit_22 = Entrada[22];
  assign Bit_23 = Entrada[23];
  assign Bit_24 = Entrada[24];
  assign Bit_25 = Entrada[25];
  assign Bit_26 = Entrada[26];
  assign Bit_27 = Entrada[27];
  assign Bit_28 = Entrada[28];
  assign Bit_29 = Entrada[29];
  assign Bit_30 = Entrada[30];
  assign Bit_31 = Entrada[31];
endmodule

// COUT-32
module COUT_32 (
  input  Bit_0,
  input  Bit_1,
  input  Bit_2,
  input  Bit_3,
  input  Bit_4,
  input  Bit_5,
  input  Bit_6,
  input  Bit_7,
  input  Bit_8,
  input  Bit_9,
  input  Bit_10,
  input  Bit_11,
  input  Bit_12,
  input  Bit_13,
  input  Bit_14,
  input  Bit_15,
  input  Bit_16,
  input  Bit_17,
  input  Bit_18,
  input  Bit_19,
  input  Bit_20,
  input  Bit_21,
  input  Bit_22,
  input  Bit_23,
  input  Bit_24,
  input  Bit_25,
  input  Bit_26,
  input  Bit_27,
  input  Bit_28,
  input  Bit_29,
  input  Bit_30,
  input  Bit_31,
  output [31:0] \Saída 
);


  assign \Saída  = {Bit_31, Bit_30, Bit_29, Bit_28, Bit_27, Bit_26, Bit_25, Bit_24, Bit_23, Bit_22, Bit_21, Bit_20, Bit_19, Bit_18, Bit_17, Bit_16, Bit_15, Bit_14, Bit_13, Bit_12, Bit_11, Bit_10, Bit_9, Bit_8, Bit_7, Bit_6, Bit_5, Bit_4, Bit_3, Bit_2, Bit_1, Bit_0};
endmodule

// SLL-32
module SLL_32 (
  input  [31:0] Entrada,
  input  Seletor,
  output [31:0] \Saída 
);

  Multiplexer #(.width(32), .enable("false")) multiplexer_1 (
    .in0(Entrada), .in1({Entrada[30:0], 1'b0}), .out(\Saída ), .sel(Seletor));
endmodule

// SRL-32
module SRL_32 (
  input  [31:0] Entrada,
  input  Seletor,
  output [31:0] \Saída 
);

  Multiplexer #(.width(32), .enable("false")) multiplexer_1 (
    .in0(Entrada), .in1({1'b0, Entrada[31:1]}), .out(\Saída ), .sel(Seletor));
endmodule

// SRA-32
module SRA_32 (
  input  [31:0] Entrada,
  input  Seletor,
  output [31:0] \Saída 
);

  Multiplexer #(.width(32), .enable("false")) multiplexer_1 (
    .in0(Entrada), .in1({{2{Entrada[31]}}, Entrada[30:1]}), .out(\Saída ), .sel(Seletor));
endmodule

// LUA-32
module LUA_32 (
  input  [31:0] Entrada,
  input  Seletor,
  output [31:0] \Saída 
);

  Multiplexer #(.width(32), .enable("false")) multiplexer_1 (
    .in0(Entrada), .in1({Entrada[15:0], {16{1'b0}}}), .out(\Saída ), .sel(Seletor));
endmodule

// SEL-SLL
module SEL_SLL_32 (
  input  [3:0] OperCode,
  output Activation
);

  and and_1 (Activation, ~OperCode[3], OperCode[2], ~OperCode[1], OperCode[0]);  // AND_Gate
endmodule

// SEL-SRL
module SEL_SRL_32 (
  input  [3:0] OperCode,
  output Activation
);

  and and_1 (Activation, ~OperCode[3], OperCode[2], OperCode[1], ~OperCode[0]);  // AND_Gate
endmodule

// SEL-SRA
module SEL_SRA_32 (
  input  [3:0] OperCode,
  output Activation
);

  and and_1 (Activation, ~OperCode[3], OperCode[2], OperCode[1], OperCode[0]);  // AND_Gate
  NOTAS notas_1 ();
endmodule

// SEL-LUA
module SEL_LUA_32 (
  input  [3:0] OperCode,
  output Activation
);

  and and_1 (Activation, OperCode[3], ~OperCode[2], ~OperCode[1], ~OperCode[0]);  // AND_Gate
endmodule

// ULA-SEL
module ULA_SEL (
  input  a,
  input  b,
  input  [3:0] OperCode,
  input  in_4,
  input  Te_SubC,
  output Result,
  output Ts_SoC,
  output Ts_SubC
);

  wire and_1_out, \complemento_2_1_saída , nand_1_out, or_1_out, sel_complemento_2_1_activation,
       somador_completo_1_soma, subtrator_completo_1_diff, xor_1_out;

  COMPLEMENTO_2 complemento_2_1 (.B(b), .\Saída (\complemento_2_1_saída ), .Seletor(sel_complemento_2_1_activation));
  Somador_Completo somador_completo_1 (
    .Ts_SoC(Ts_SoC), .Te_SoC(in_4), .Soma(somador_completo_1_soma), .a(a), .b(\complemento_2_1_saída ));
  Subtrator_Completo subtrator_completo_1 (
    .Ts_SubC(Ts_SubC), .Te_SubC(Te_SubC), .Diff(subtrator_completo_1_diff), .a(a), .b(b));
  and and_1 (and_1_out, b, a);
  or or_1 (or_1_out, b, a);
  xor xor_1 (xor_1_out, b, a);
  nand nand_1 (nand_1_out, a, b);
  SEL_COMPLEMENTO_2 sel_complemento_2_1 (.Activation(sel_complemento_2_1_activation), .OperCode(OperCode));
  MUX_16 mux_16_1 (
    .Canal_0(and_1_out), .Canal_1(or_1_out), .Canal_2(xor_1_out), .Canal_3(somador_completo_1_soma),
    .Canal_4(subtrator_completo_1_diff), .Canal_5(b), .Canal_6(b), .Canal_7(b), .Canal_8(a),
    .Canal_9(nand_1_out), .Canal_15(somador_completo_1_soma), .\Saída (Result), .Sel_3(OperCode[3]),
    .Sel2(OperCode[2]), .Sel1(OperCode[1]), .Sel_0(OperCode[0]));  // open: Canal_10, Canal_11, Canal_12, Canal_13, Canal_14
endmodule

// ULA-32
module ULA_32 (
  input  [31:0] A,
  input  [31:0] B,
  input  [3:0] OperCode,
  output [31:0] Result
);

  wire _0_result, _0_ts_soc, _0_ts_subc, _1_result, _1_ts_soc, _1_ts_subc, _2_result, _2_ts_soc, _2_ts_subc,
       _3_result, _3_ts_soc, _3_ts_subc, _4_result, _4_ts_soc, _4_ts_subc, _5_result, _5_ts_soc, _5_ts_subc,
       _6_result, _6_ts_soc, _6_ts_subc, _7_result, _7_ts_soc, _7_ts_subc, _8_result, _8_ts_soc, _8_ts_subc,
       _9_result, _9_ts_soc, _9_ts_subc, _10_result, _10_ts_soc, _10_ts_subc, _11_result, _11_ts_soc,
       _11_ts_subc, _12_result, _12_ts_soc, _12_ts_subc, _13_result, _13_ts_soc, _13_ts_subc, _14_result,
       _14_ts_soc, _14_ts_subc, _15_result, _15_ts_soc, _15_ts_subc, _16_result, _16_ts_soc, _16_ts_subc,
       _17_result, _17_ts_soc, _17_ts_subc, _18_result, _18_ts_soc, _18_ts_subc, _19_result, _19_ts_soc,
       _19_ts_subc, _20_result, _20_ts_soc, _20_ts_subc, _21_result, _21_ts_soc, _21_ts_subc, _22_result,
       _22_ts_soc, _22_ts_subc, _23_result, _23_ts_soc, _23_ts_subc, _24_result, _24_ts_soc, _24_ts_subc,
       _25_result, _25_ts_soc, _25_ts_subc, _26_result, _26_ts_soc, _26_ts_subc, _27_result, _27_ts_soc,
       _27_ts_subc, _28_result, _28_ts_soc, _28_ts_subc, _29_result, _29_ts_soc, _29_ts_subc, _30_result,
       _30_ts_soc, _30_ts_subc, _31_result, A_bit_0, A_bit_1, A_bit_2, A_bit_3, A_bit_4, A_bit_5, A_bit_6,
       A_bit_7, A_bit_8, A_bit_9, A_bit_10, A_bit_11, A_bit_12, A_bit_13, A_bit_14, A_bit_15, A_bit_16,
       A_bit_17, A_bit_18, A_bit_19, A_bit_20, A_bit_21, A_bit_22, A_bit_23, A_bit_24, A_bit_25, A_bit_26,
       A_bit_27, A_bit_28, A_bit_29, A_bit_30, A_bit_31, B_bit_0, B_bit_1, B_bit_2, B_bit_3, B_bit_4,
       B_bit_5, B_bit_6, B_bit_7, B_bit_8, B_bit_9, B_bit_10, B_bit_11, B_bit_12, B_bit_13, B_bit_14,
       B_bit_15, B_bit_16, B_bit_17, B_bit_18, B_bit_19, B_bit_20, B_bit_21, B_bit_22, B_bit_23, B_bit_24,
       B_bit_25, B_bit_26, B_bit_27, B_bit_28, B_bit_29, B_bit_30, B_bit_31, sel_complemento_2_1_activation,
       sel_lua_32_1_activation, sel_sll_32_1_activation, sel_sra_32_1_activation, sel_srl_32_1_activation;
  wire [31:0] \lua_32_1_saída , \sll_32_1_saída , \sra_32_1_saída , \srl_32_1_saída ;

  SEL_SLL_32 sel_sll_32_1 (.Activation(sel_sll_32_1_activation), .OperCode(OperCode));
  SEL_LUA_32 sel_lua_32_1 (.Activation(sel_lua_32_1_activation), .OperCode(OperCode));
  SLL_32 sll_32_1 (.Entrada(B), .\Saída (\sll_32_1_saída ), .Seletor(sel_sll_32_1_activation));
  SEL_SRL_32 sel_srl_32_1 (.Activation(sel_srl_32_1_activation), .OperCode(OperCode));
  LUA_32 lua_32_1 (.Entrada(A), .\Saída (\lua_32_1_saída ), .Seletor(sel_lua_32_1_activation));
  SRL_32 srl_32_1 (.Entrada(\sll_32_1_saída ), .\Saída (\srl_32_1_saída ), .Seletor(sel_srl_32_1_activation));
  SEL_SRA_32 sel_sra_32_1 (.Activation(sel_sra_32_1_activation), .OperCode(OperCode));
  SRA_32 sra_32_1 (.Entrada(\srl_32_1_saída ), .\Saída (\sra_32_1_saída ), .Seletor(sel_sra_32_1_activation));
  CIN_32 u_A (
    .Entrada(\lua_32_1_saída ), .Bit_0(A_bit_0), .Bit_1(A_bit_1), .Bit_2(A_bit_2), .Bit_3(A_bit_3),
    .Bit_4(A_bit_4), .Bit_5(A_bit_5), .Bit_6(A_bit_6), .Bit_7(A_bit_7), .Bit_8(A_bit_8), .Bit_9(A_bit_9),
    .Bit_10(A_bit_10), .Bit_11(A_bit_11), .Bit_12(A_bit_12), .Bit_13(A_bit_13), .Bit_14(A_bit_14),
    .Bit_15(A_bit_15), .Bit_16(A_bit_16), .Bit_17(A_bit_17), .Bit_18(A_bit_18), .Bit_19(A_bit_19),
    .Bit_20(A_bit_20), .Bit_21(A_bit_21), .Bit_22(A_bit_22), .Bit_23(A_bit_23), .Bit_24(A_bit_24),
    .Bit_25(A_bit_25), .Bit_26(A_bit_26), .Bit_27(A_bit_27), .Bit_28(A_bit_28), .Bit_29(A_bit_29),
    .Bit_30(A_bit_30), .Bit_31(A_bit_31));
  CIN_32 u_B (
    .Entrada(\sra_32_1_saída ), .Bit_0(B_bit_0), .Bit_1(B_bit_1), .Bit_2(B_bit_2), .Bit_3(B_bit_3),
    .Bit_4(B_bit_4), .Bit_5(B_bit_5), .Bit_6(B_bit_6), .Bit_7(B_bit_7), .Bit_8(B_bit_8), .Bit_9(B_bit_9),
    .Bit_10(B_bit_10), .Bit_11(B_bit_11), .Bit_12(B_bit_12), .Bit_13(B_bit_13), .Bit_14(B_bit_14),
    .Bit_15(B_bit_15), .Bit_16(B_bit_16), .Bit_17(B_bit_17), .Bit_18(B_bit_18), .Bit_19(B_bit_19),
    .Bit_20(B_bit_20), .Bit_21(B_bit_21), .Bit_22(B_bit_22), .Bit_23(B_bit_23), .Bit_24(B_bit_24),
    .Bit_25(B_bit_25), .Bit_26(B_bit_26), .Bit_27(B_bit_27), .Bit_28(B_bit_28), .Bit_29(B_bit_29),
    .Bit_30(B_bit_30), .Bit_31(B_bit_31));
  ULA_SEL _15 (
    .Ts_SoC(_15_ts_soc), .Ts_SubC(_15_ts_subc), .Te_SubC(_14_ts_subc), .a(A_bit_15), .b(B_bit_15),
    .OperCode(OperCode), .Result(_15_result), .in_4(_14_ts_soc));
  ULA_SEL _31 (
    .Te_SubC(_30_ts_subc), .a(A_bit_31), .b(B_bit_31), .OperCode(OperCode), .Result(_31_result),
    .in_4(_30_ts_soc));  // open: Ts_SoC, Ts_SubC
  ULA_SEL _14 (
    .Ts_SoC(_14_ts_soc), .Ts_SubC(_14_ts_subc), .Te_SubC(_13_ts_subc), .a(A_bit_14), .b(B_bit_14),
    .OperCode(OperCode), .Result(_14_result), .in_4(_13_ts_soc));
  ULA_SEL _30 (
    .Ts_SoC(_30_ts_soc), .Ts_SubC(_30_ts_subc), .Te_SubC(_29_ts_subc), .a(A_bit_30), .b(B_bit_30),
    .OperCode(OperCode), .Result(_30_result), .in_4(_29_ts_soc));
  ULA_SEL _13 (
    .Ts_SoC(_13_ts_soc), .Ts_SubC(_13_ts_subc), .Te_SubC(_12_ts_subc), .a(A_bit_13), .b(B_bit_13),
    .OperCode(OperCode), .Result(_13_result), .in_4(_12_ts_soc));
  ULA_SEL _29 (
    .Ts_SoC(_29_ts_soc), .Ts_SubC(_29_ts_subc), .Te_SubC(_28_ts_subc), .a(A_bit_29), .b(B_bit_29),
    .OperCode(OperCode), .Result(_29_result), .in_4(_28_ts_soc));
  ULA_SEL _12 (
    .Ts_SoC(_12_ts_soc), .Ts_SubC(_12_ts_subc), .Te_SubC(_11_ts_subc), .a(A_bit_12), .b(B_bit_12),
    .OperCode(OperCode), .Result(_12_result), .in_4(_11_ts_soc));
  ULA_SEL _28 (
    .Ts_SoC(_28_ts_soc), .Ts_SubC(_28_ts_subc), .Te_SubC(_27_ts_subc), .a(A_bit_28), .b(B_bit_28),
    .OperCode(OperCode), .Result(_28_result), .in_4(_27_ts_soc));
  ULA_SEL _11 (
    .Ts_SoC(_11_ts_soc), .Ts_SubC(_11_ts_subc), .Te_SubC(_10_ts_subc), .a(A_bit_11), .b(B_bit_11),
    .OperCode(OperCode), .Result(_11_result), .in_4(_10_ts_soc));
  ULA_SEL _27 (
    .Ts_SoC(_27_ts_soc), .Ts_SubC(_27_ts_subc), .Te_SubC(_26_ts_subc), .a(A_bit_27), .b(B_bit_27),
    .OperCode(OperCode), .Result(_27_result), .in_4(_26_ts_soc));
  ULA_SEL _10 (
    .Ts_SoC(_10_ts_soc), .Ts_SubC(_10_ts_subc), .Te_SubC(_9_ts_subc), .a(A_bit_10), .b(B_bit_10),
    .OperCode(OperCode), .Result(_10_result), .in_4(_9_ts_soc));
  ULA_SEL _26 (
    .Ts_SoC(_26_ts_soc), .Ts_SubC(_26_ts_subc), .Te_SubC(_25_ts_subc), .a(A_bit_26), .b(B_bit_26),
    .OperCode(OperCode), .Result(_26_result), .in_4(_25_ts_soc));
  ULA_SEL _9 (
    .Ts_SoC(_9_ts_soc), .Ts_SubC(_9_ts_subc), .Te_SubC(_8_ts_subc), .a(A_bit_9), .b(B_bit_9),
    .OperCode(OperCode), .Result(_9_result), .in_4(_8_ts_soc));
  ULA_SEL _25 (
    .Ts_SoC(_25_ts_soc), .Ts_SubC(_25_ts_subc), .Te_SubC(_24_ts_subc), .a(A_bit_25), .b(B_bit_25),
    .OperCode(OperCode), .Result(_25_result), .in_4(_24_ts_soc));
  ULA_SEL _8 (
    .Ts_SoC(_8_ts_soc), .Ts_SubC(_8_ts_subc), .Te_SubC(_7_ts_subc), .a(A_bit_8), .b(B_bit_8),
    .OperCode(OperCode), .Result(_8_result), .in_4(_7_ts_soc));
  ULA_SEL _24 (
    .Ts_SoC(_24_ts_soc), .Ts_SubC(_24_ts_subc), .Te_SubC(_23_ts_subc), .a(A_bit_24), .b(B_bit_24),
    .OperCode(OperCode), .Result(_24_result), .in_4(_23_ts_soc));
  ULA_SEL _7 (
    .Ts_SoC(_7_ts_soc), .Ts_SubC(_7_ts_subc), .Te_SubC(_6_ts_subc), .a(A_bit_7), .b(B_bit_7),
    .OperCode(OperCode), .Result(_7_result), .in_4(_6_ts_soc));
  ULA_SEL _23 (
    .Ts_SoC(_23_ts_soc), .Ts_SubC(_23_ts_subc), .Te_SubC(_22_ts_subc), .a(A_bit_23), .b(B_bit_23),
    .OperCode(OperCode), .Result(_23_result), .in_4(_22_ts_soc));
  ULA_SEL _6 (
    .Ts_SoC(_6_ts_soc), .Ts_SubC(_6_ts_subc), .Te_SubC(_5_ts_subc), .a(A_bit_6), .b(B_bit_6),
    .OperCode(OperCode), .Result(_6_result), .in_4(_5_ts_soc));
  ULA_SEL _22 (
    .Ts_SoC(_22_ts_soc), .Ts_SubC(_22_ts_subc), .Te_SubC(_21_ts_subc), .a(A_bit_22), .b(B_bit_22),
    .OperCode(OperCode), .Result(_22_result), .in_4(_21_ts_soc));
  ULA_SEL _5 (
    .Ts_SoC(_5_ts_soc), .Ts_SubC(_5_ts_subc), .Te_SubC(_4_ts_subc), .a(A_bit_5), .b(B_bit_5),
    .OperCode(OperCode), .Result(_5_result), .in_4(_4_ts_soc));
  ULA_SEL _21 (
    .Ts_SoC(_21_ts_soc), .Ts_SubC(_21_ts_subc), .Te_SubC(_20_ts_subc), .a(A_bit_21), .b(B_bit_21),
    .OperCode(OperCode), .Result(_21_result), .in_4(_20_ts_soc));
  ULA_SEL _4 (
    .Ts_SoC(_4_ts_soc), .Ts_SubC(_4_ts_subc), .Te_SubC(_3_ts_subc), .a(A_bit_4), .b(B_bit_4),
    .OperCode(OperCode), .Result(_4_result), .in_4(_3_ts_soc));
  ULA_SEL _20 (
    .Ts_SoC(_20_ts_soc), .Ts_SubC(_20_ts_subc), .Te_SubC(_19_ts_subc), .a(A_bit_20), .b(B_bit_20),
    .OperCode(OperCode), .Result(_20_result), .in_4(_19_ts_soc));
  ULA_SEL _3 (
    .Ts_SoC(_3_ts_soc), .Ts_SubC(_3_ts_subc), .Te_SubC(_2_ts_subc), .a(A_bit_3), .b(B_bit_3),
    .OperCode(OperCode), .Result(_3_result), .in_4(_2_ts_soc));
  ULA_SEL _19 (
    .Ts_SoC(_19_ts_soc), .Ts_SubC(_19_ts_subc), .Te_SubC(_18_ts_subc), .a(A_bit_19), .b(B_bit_19),
    .OperCode(OperCode), .Result(_19_result), .in_4(_18_ts_soc));
  ULA_SEL _2 (
    .Ts_SoC(_2_ts_soc), .Ts_SubC(_2_ts_subc), .Te_SubC(_1_ts_subc), .a(A_bit_2), .b(B_bit_2),
    .OperCode(OperCode), .Result(_2_result), .in_4(_1_ts_soc));
  ULA_SEL _18 (
    .Ts_SoC(_18_ts_soc), .Ts_SubC(_18_ts_subc), .Te_SubC(_17_ts_subc), .a(A_bit_18), .b(B_bit_18),
    .OperCode(OperCode), .Result(_18_result), .in_4(_17_ts_soc));
  ULA_SEL _1 (
    .Ts_SoC(_1_ts_soc), .Ts_SubC(_1_ts_subc), .Te_SubC(_0_ts_subc), .a(A_bit_1), .b(B_bit_1),
    .OperCode(OperCode), .Result(_1_result), .in_4(_0_ts_soc));
  ULA_SEL _17 (
    .Ts_SoC(_17_ts_soc), .Ts_SubC(_17_ts_subc), .Te_SubC(_16_ts_subc), .a(A_bit_17), .b(B_bit_17),
    .OperCode(OperCode), .Result(_17_result), .in_4(_16_ts_soc));
  ULA_SEL _0 (
    .Ts_SoC(_0_ts_soc), .Ts_SubC(_0_ts_subc), .Te_SubC(sel_complemento_2_1_activation), .a(A_bit_0),
    .b(B_bit_0), .OperCode(OperCode), .Result(_0_result), .in_4(sel_complemento_2_1_activation));
  ULA_SEL _16 (
    .Ts_SoC(_16_ts_soc), .Ts_SubC(_16_ts_subc), .Te_SubC(_15_ts_subc), .a(A_bit_16), .b(B_bit_16),
    .OperCode(OperCode), .Result(_16_result), .in_4(_15_ts_soc));
  SEL_COMPLEMENTO_2 sel_complemento_2_1 (.Activation(sel_complemento_2_1_activation), .OperCode(OperCode));
  COUT_32 cout_32_1 (
    .Bit_0(_0_result), .Bit_1(_1_result), .Bit_2(_2_result), .Bit_3(_3_result), .Bit_4(_4_result),
    .Bit_5(_5_result), .Bit_6(_6_result), .Bit_7(_7_result), .Bit_8(_8_result), .Bit_9(_9_result),
    .Bit_10(_10_result), .Bit_11(_11_result), .Bit_12(_12_result), .Bit_13(_13_result), .Bit_14(_14_result),
    .Bit_15(_15_result), .Bit_16(_16_result), .Bit_17(_17_result), .Bit_18(_18_result), .Bit_19(_19_result),
    .Bit_20(_20_result), .Bit_21(_21_result), .Bit_22(_22_result), .Bit_23(_23_result), .Bit_24(_24_result),
    .Bit_25(_25_result), .Bit_26(_26_result), .Bit_27(_27_result), .Bit_28(_28_result), .Bit_29(_29_result),
    .Bit_30(_30_result), .Bit_31(_31_result), .\Saída (Result));
endmodule

// Registrador-32
module Registrador_32 (
  input  WR,
  input  [31:0] CIN,
  output [31:0] COUT
);

  wire _0_q, _1_q, _2_q, _3_q, _4_q, _5_q, _6_q, _7_q, _8_q, _9_q, _10_q, _11_q, _12_q, _13_q, _14_q, _15_q,
       _16_q, _17_q, _18_q, _19_q, _20_q, _21_q, _22_q, _23_q, _24_q, _25_q, _26_q, _27_q, _28_q, _29_q,
       _30_q, _31_q, Entrada_bit_0, Entrada_bit_1, Entrada_bit_2, Entrada_bit_3, Entrada_bit_4,
       Entrada_bit_5, Entrada_bit_6, Entrada_bit_7, Entrada_bit_8, Entrada_bit_9, Entrada_bit_10,
       Entrada_bit_11, Entrada_bit_12, Entrada_bit_13, Entrada_bit_14, Entrada_bit_15, Entrada_bit_16,
       Entrada_bit_17, Entrada_bit_18, Entrada_bit_19, Entrada_bit_20, Entrada_bit_21, Entrada_bit_22,
       Entrada_bit_23, Entrada_bit_24, Entrada_bit_25, Entrada_bit_26, Entrada_bit_27, Entrada_bit_28,
       Entrada_bit_29, Entrada_bit_30, Entrada_bit_31;

  CIN_32 Entrada (
    .Entrada(CIN), .Bit_0(Entrada_bit_0), .Bit_1(Entrada_bit_1), .Bit_2(Entrada_bit_2),
    .Bit_3(Entrada_bit_3), .Bit_4(Entrada_bit_4), .Bit_5(Entrada_bit_5), .Bit_6(Entrada_bit_6),
    .Bit_7(Entrada_bit_7), .Bit_8(Entrada_bit_8), .Bit_9(Entrada_bit_9), .Bit_10(Entrada_bit_10),
    .Bit_11(Entrada_bit_11), .Bit_12(Entrada_bit_12), .Bit_13(Entrada_bit_13), .Bit_14(Entrada_bit_14),
    .Bit_15(Entrada_bit_15), .Bit_16(Entrada_bit_16), .Bit_17(Entrada_bit_17), .Bit_18(Entrada_bit_18),
    .Bit_19(Entrada_bit_19), .Bit_20(Entrada_bit_20), .Bit_21(Entrada_bit_21), .Bit_22(Entrada_bit_22),
    .Bit_23(Entrada_bit_23), .Bit_24(Entrada_bit_24), .Bit_25(Entrada_bit_25), .Bit_26(Entrada_bit_26),
    .Bit_27(Entrada_bit_27), .Bit_28(Entrada_bit_28), .Bit_29(Entrada_bit_29), .Bit_30(Entrada_bit_30),
    .Bit_31(Entrada_bit_31));
  D_Flip_Flop _15 (.clk(WR), .D(Entrada_bit_15), .Q(_15_q));  // open: Qn, preset, en, reset
  D_Flip_Flop _31 (.clk(WR), .D(Entrada_bit_31), .Q(_31_q));  // open: Qn, preset, en, reset
  D_Flip_Flop _14 (.clk(WR), .D(Entrada_bit_14), .Q(_14_q));  // open: Qn, preset, en, reset
  D_Flip_Flop _30 (.clk(WR), .D(Entrada_bit_30), .Q(_30_q));  // open: Qn, preset, en, reset
  D_Flip_Flop _13 (.clk(WR), .D(Entrada_bit_13), .Q(_13_q));  // open: Qn, preset, en, reset
  D_Flip_Flop _29 (.clk(WR), .D(Entrada_bit_29), .Q(_29_q));  // open: Qn, preset, en, reset
  D_Flip_Flop _12 (.clk(WR), .D(Entrada_bit_12), .Q(_12_q));  // open: Qn, preset, en, reset
  D_Flip_Flop _28 (.clk(WR), .D(Entrada_bit_28), .Q(_28_q));  // open: Qn, preset, en, reset
  D_Flip_Flop _11 (.clk(WR), .D(Entrada_bit_11), .Q(_11_q));  // open: Qn, preset, en, reset
  D_Flip_Flop _27 (.clk(WR), .D(Entrada_bit_27), .Q(_27_q));  // open: Qn, preset, en, reset
  D_Flip_Flop _10 (.clk(WR), .D(Entrada_bit_10), .Q(_10_q));  // open: Qn, preset, en, reset
  D_Flip_Flop _26 (.clk(WR), .D(Entrada_bit_26), .Q(_26_q));  // open: Qn, preset, en, reset
  D_Flip_Flop _9 (.clk(WR), .D(Entrada_bit_9), .Q(_9_q));  // open: Qn, preset, en, reset
  D_Flip_Flop _25 (.clk(WR), .D(Entrada_bit_25), .Q(_25_q));  // open: Qn, preset, en, reset
  D_Flip_Flop _8 (.clk(WR), .D(Entrada_bit_8), .Q(_8_q));  // open: Qn, preset, en, reset
  D_Flip_Flop _24 (.clk(WR), .D(Entrada_bit_24), .Q(_24_q));  // open: Qn, preset, en, reset
  D_Flip_Flop _7 (.clk(WR), .D(Entrada_bit_7), .Q(_7_q));  // open: Qn, preset, en, reset
  D_Flip_Flop _23 (.clk(WR), .D(Entrada_bit_23), .Q(_23_q));  // open: Qn, preset, en, reset
  D_Flip_Flop _6 (.clk(WR), .D(Entrada_bit_6), .Q(_6_q));  // open: Qn, preset, en, reset
  D_Flip_Flop _22 (.clk(WR), .D(Entrada_bit_22), .Q(_22_q));  // open: Qn, preset, en, reset
  D_Flip_Flop _5 (.clk(WR), .D(Entrada_bit_5), .Q(_5_q));  // open: Qn, preset, en, reset
  D_Flip_Flop _21 (.clk(WR), .D(Entrada_bit_21), .Q(_21_q));  // open: Qn, preset, en, reset
  D_Flip_Flop _4 (.clk(WR), .D(Entrada_bit_4), .Q(_4_q));  // open: Qn, preset, en, reset
  D_Flip_Flop _20 (.clk(WR), .D(Entrada_bit_20), .Q(_20_q));  // open: Qn, preset, en, reset
  D_Flip_Flop _3 (.clk(WR), .D(Entrada_bit_3), .Q(_3_q));  // open: Qn, preset, en, reset
  D_Flip_Flop _19 (.clk(WR), .D(Entrada_bit_19), .Q(_19_q));  // open: Qn, preset, en, reset
  D_Flip_Flop _2 (.clk(WR), .D(Entrada_bit_2), .Q(_2_q));  // open: Qn, preset, en, reset
  D_Flip_Flop _18 (.clk(WR), .D(Entrada_bit_18), .Q(_18_q));  // open: Qn, preset, en, reset
  D_Flip_Flop _1 (.clk(WR), .D(Entrada_bit_1), .Q(_1_q));  // open: Qn, preset, en, reset
  D_Flip_Flop _17 (.clk(WR), .D(Entrada_bit_17), .Q(_17_q));  // open: Qn, preset, en, reset
  D_Flip_Flop _0 (.clk(WR), .D(Entrada_bit_0), .Q(_0_q));  // open: Qn, preset, en, reset
  D_Flip_Flop _16 (.clk(WR), .D(Entrada_bit_16), .Q(_16_q));  // open: Qn, preset, en, reset
  COUT_32 cout_32_1 (
    .Bit_0(_0_q), .Bit_1(_1_q), .Bit_2(_2_q), .Bit_3(_3_q), .Bit_4(_4_q), .Bit_5(_5_q), .Bit_6(_6_q),
    .Bit_7(_7_q), .Bit_8(_8_q), .Bit_9(_9_q), .Bit_10(_10_q), .Bit_11(_11_q), .Bit_12(_12_q), .Bit_13(_13_q),
    .Bit_14(_14_q), .Bit_15(_15_q), .Bit_16(_16_q), .Bit_17(_17_q), .Bit_18(_18_q), .Bit_19(_19_q),
    .Bit_20(_20_q), .Bit_21(_21_q), .Bit_22(_22_q), .Bit_23(_23_q), .Bit_24(_24_q), .Bit_25(_25_q),
    .Bit_26(_26_q), .Bit_27(_27_q), .Bit_28(_28_q), .Bit_29(_29_q), .Bit_30(_30_q), .Bit_31(_31_q),
    .\Saída (COUT));
endmodule

// Banco-Registrador-32
module Banco_Registrador_32 (
  input  [31:0] DATA_IN_32,
  input  [4:0] SelRegA,
  input  [4:0] SelRegB,
  input  WR,
  input  [4:0] SelRegW,
  output [31:0] DataRegA,
  output [31:0] DataRegB
);

  wire demultiplexer_1_out0, demultiplexer_1_out1, demultiplexer_1_out2, demultiplexer_1_out3,
       demultiplexer_1_out4, demultiplexer_1_out5, demultiplexer_1_out6, demultiplexer_1_out7,
       demultiplexer_1_out8, demultiplexer_1_out9, demultiplexer_1_out10, demultiplexer_1_out11,
       demultiplexer_1_out12, demultiplexer_1_out13, demultiplexer_1_out14, demultiplexer_1_out15,
       demultiplexer_1_out16, demultiplexer_1_out17, demultiplexer_1_out18, demultiplexer_1_out19,
       demultiplexer_1_out20, demultiplexer_1_out21, demultiplexer_1_out22, demultiplexer_1_out23,
       demultiplexer_1_out24, demultiplexer_1_out25, demultiplexer_1_out26, demultiplexer_1_out27,
       demultiplexer_1_out28, demultiplexer_1_out29, demultiplexer_1_out30, demultiplexer_1_out31;
  wire [31:0] _0_cout, _1_cout, _2_cout, _3_cout, _4_cout, _5_cout, _6_cout, _7_cout, _8_cout, _9_cout,
       _10_cout, _11_cout, _12_cout, _13_cout, _14_cout, _15_cout, _16_cout, _17_cout, _18_cout, _19_cout,
       _20_cout, _21_cout, _22_cout, _23_cout, _24_cout, _25_cout, _26_cout, _27_cout, _28_cout, _29_cout,
       _30_cout, _31_cout;

  Demultiplexer #(.select(5), .enable("false")) demultiplexer_1 (
    .out0(demultiplexer_1_out0), .out1(demultiplexer_1_out1), .out2(demultiplexer_1_out2),
    .out3(demultiplexer_1_out3), .out4(demultiplexer_1_out4), .out5(demultiplexer_1_out5),
    .out6(demultiplexer_1_out6), .out7(demultiplexer_1_out7), .out8(demultiplexer_1_out8),
    .out9(demultiplexer_1_out9), .out10(demultiplexer_1_out10), .out11(demultiplexer_1_out11),
    .out12(demultiplexer_1_out12), .out13(demultiplexer_1_out13), .out14(demultiplexer_1_out14),
    .out15(demultiplexer_1_out15), .out16(demultiplexer_1_out16), .out17(demultiplexer_1_out17),
    .out18(demultiplexer_1_out18), .out19(demultiplexer_1_out19), .out20(demultiplexer_1_out20),
    .out21(demultiplexer_1_out21), .out22(demultiplexer_1_out22), .out23(demultiplexer_1_out23),
    .out24(demultiplexer_1_out24), .out25(demultiplexer_1_out25), .out26(demultiplexer_1_out26),
    .out27(demultiplexer_1_out27), .out28(demultiplexer_1_out28), .out29(demultiplexer_1_out29),
    .out30(demultiplexer_1_out30), .out31(demultiplexer_1_out31), .in(WR), .sel(SelRegW));
  Registrador_32 _0 (.WR(demultiplexer_1_out0), .CIN(DATA_IN_32), .COUT(_0_cout));
  Registrador_32 _1 (.WR(demultiplexer_1_out1), .CIN(DATA_IN_32), .COUT(_1_cout));
  Registrador_32 _2 (.WR(demultiplexer_1_out2), .CIN(DATA_IN_32), .COUT(_2_cout));
  Registrador_32 _3 (.WR(demultiplexer_1_out3), .CIN(DATA_IN_32), .COUT(_3_cout));
  Registrador_32 _4 (.WR(demultiplexer_1_out4), .CIN(DATA_IN_32), .COUT(_4_cout));
  Registrador_32 _5 (.WR(demultiplexer_1_out5), .CIN(DATA_IN_32), .COUT(_5_cout));
  Registrador_32 _6 (.WR(demultiplexer_1_out6), .CIN(DATA_IN_32), .COUT(_6_cout));
  Registrador_32 _7 (.WR(demultiplexer_1_out7), .CIN(DATA_IN_32), .COUT(_7_cout));
  Registrador_32 _8 (.WR(demultiplexer_1_out8), .CIN(DATA_IN_32), .COUT(_8_cout));
  Registrador_32 _9 (.WR(demultiplexer_1_out9), .CIN(DATA_IN_32), .COUT(_9_cout));
  Registrador_32 _10 (.WR(demultiplexer_1_out10), .CIN(DATA_IN_32), .COUT(_10_cout));
  Registrador_32 _11 (.WR(demultiplexer_1_out11), .CIN(DATA_IN_32), .COUT(_11_cout));
  Registrador_32 _12 (.WR(demultiplexer_1_out12), .CIN(DATA_IN_32), .COUT(_12_cout));
  Registrador_32 _13 (.WR(demultiplexer_1_out13), .CIN(DATA_IN_32), .COUT(_13_cout));
  Registrador_32 _14 (.WR(demultiplexer_1_out14), .CIN(DATA_IN_32), .COUT(_14_cout));
  Registrador_32 _15 (.WR(demultiplexer_1_out15), .CIN(DATA_IN_32), .COUT(_15_cout));
  Registrador_32 _16 (.WR(demultiplexer_1_out16), .CIN(DATA_IN_32), .COUT(_16_cout));
  Registrador_32 _17 (.WR(demultiplexer_1_out17), .CIN(DATA_IN_32), .COUT(_17_cout));
  Registrador_32 _18 (.WR(demultiplexer_1_out18), .CIN(DATA_IN_32), .COUT(_18_cout));
  Registrador_32 _19 (.WR(demultiplexer_1_out19), .CIN(DATA_IN_32), .COUT(_19_cout));
  Registrador_32 _20 (.WR(demultiplexer_1_out20), .CIN(DATA_IN_32), .COUT(_20_cout));
  Registrador_32 _21 (.WR(demultiplexer_1_out21), .CIN(DATA_IN_32), .COUT(_21_cout));
  Registrador_32 _22 (.WR(demultiplexer_1_out22), .CIN(DATA_IN_32), .COUT(_22_cout));
  Registrador_32 _23 (.WR(demultiplexer_1_out23), .CIN(DATA_IN_32), .COUT(_23_cout));
  Registrador_32 _24 (.WR(demultiplexer_1_out24), .CIN(DATA_IN_32), .COUT(_24_cout));
  Registrador_32 _25 (.WR(demultiplexer_1_out25), .CIN(DATA_IN_32), .COUT(_25_cout));
  Registrador_32 _26 (.WR(demultiplexer_1_out26), .CIN(DATA_IN_32), .COUT(_26_cout));
  Registrador_32 _27 (.WR(demultiplexer_1_out27), .CIN(DATA_IN_32), .COUT(_27_cout));
  Registrador_32 _28 (.WR(demultiplexer_1_out28), .CIN(DATA_IN_32), .COUT(_28_cout));
  Registrador_32 _29 (.WR(demultiplexer_1_out29), .CIN(DATA_IN_32), .COUT(_29_cout));
  Registrador_32 _30 (.WR(demultiplexer_1_out30), .CIN(DATA_IN_32), .COUT(_30_cout));
  Registrador_32 _31 (.WR(demultiplexer_1_out31), .CIN(DATA_IN_32), .COUT(_31_cout));
  Multiplexer #(.select(5), .width(32), .enable("false")) multiplexer_1 (
    .in0(_0_cout), .in1(_1_cout), .in2(_2_cout), .in3(_3_cout), .in4(_4_cout), .in5(_5_cout), .in6(_6_cout),
    .in7(_7_cout), .in8(_8_cout), .in9(_9_cout), .in10(_10_cout), .in11(_11_cout), .in12(_12_cout),
    .in13(_13_cout), .in14(_14_cout), .in15(_15_cout), .in16(_16_cout), .in17(_17_cout), .in18(_18_cout),
    .in19(_19_cout), .in20(_20_cout), .in21(_21_cout), .in22(_22_cout), .in23(_23_cout), .in24(_24_cout),
    .in25(_25_cout), .in26(_26_cout), .in27(_27_cout), .in28(_28_cout), .in29(_29_cout), .in30(_30_cout),
    .in31(_31_cout), .out(DataRegA), .sel(SelRegA));
  Multiplexer #(.select(5), .width(32), .enable("false")) multiplexer_2 (
    .in0(_0_cout), .in1(_1_cout), .in2(_2_cout), .in3(_3_cout), .in4(_4_cout), .in5(_5_cout), .in6(_6_cout),
    .in7(_7_cout), .in8(_8_cout), .in9(_9_cout), .in10(_10_cout), .in11(_11_cout), .in12(_12_cout),
    .in13(_13_cout), .in14(_14_cout), .in15(_15_cout), .in16(_16_cout), .in17(_17_cout), .in18(_18_cout),
    .in19(_19_cout), .in20(_20_cout), .in21(_21_cout), .in22(_22_cout), .in23(_23_cout), .in24(_24_cout),
    .in25(_25_cout), .in26(_26_cout), .in27(_27_cout), .in28(_28_cout), .in29(_29_cout), .in30(_30_cout),
    .in31(_31_cout), .out(DataRegB), .sel(SelRegB));
endmodule
